// Digital circuit Ben Eater's SAP.dig as structural Verilog
module Ben_Eater_s_SAP (
  input  clk,
  input  clk_2,
  input  in_3
);

  wire add_2_c_o, AI, and_1_out, and_2_out, and_3_out, and_5_out, and_6_out, and_7_out, and_8_out, and_9_out,
       AO, AR0, AR1, AR2, AR3, AR4, AR5, AR6, AR7, B0, B1, B2, B3, B4, B5, B6, B7, BI, BR0, BR1, BR2, BR3,
       BR4, BR5, BR6, BR7, button_2_out, CE, CF, CFO, CLK_t, CO, decoder_1_out_0, decoder_1_out_1,
       decoder_1_out_2, decoder_1_out_3, decoder_1_out_4, decoder_1_out_5, decoder_1_out_6, decoder_1_out_7,
       decoder_2_out_0, decoder_2_out_1, decoder_2_out_2, decoder_2_out_3, driver_10_out, EO, FI, HLT, II,
       IO, IR0, IR1, IR2, IR3, IR4, IR5, IR6, IR7, JMP, LL0, LL1, LL2, LL3, LL4, LL5, LL6, LL7, MA0, MA1,
       MA2, MA3, MANR, MAR0, MAR1, MAR2, MAR3, MD0, MD1, MD2, MD3, MD4, MD5, MD6, MD7, MI, nCLK, not_1_out,
       not_2_out, not_3_out, not_4_out, not_6_out, not_15_out, not_16_out, not_17_out, not_18_out, nRUN, OI,
       or_1_out, RAM0, RAM1, RAM2, RAM3, RAM4, RAM5, RAM6, RAM7, RI, RMI, RO, RST, SU, switch_2_b, T0, T1,
       T2, T3, T4, T5, T6, T7, xor_1_out, ZF, ZFO;
  wire [1:0] jk_ff_1_q;
  wire [2:0] TC;
  wire [3:0] counterpreset_1_out, d_ff_as_3_q, RMH, RML, xor_6_out, xor_8_out;
  wire [3:2] d_ff_as_6_q;
  wire [7:0] d_ff_as_9_q, eeprom_1_d;

  Multiplexer multiplexer_1 (.sel(nRUN), .in_0(RI), .in_1(MANR), .out(RMI));
  Button button_1 (.out(MANR));
  Button button_2 (.out(button_2_out));
  assign B0 = RO ? RAM0 : 1'bz;  // Driver driver_1
  RAMDualPort #(.AddrBits(4), .Bits(4)) ramdualport_1 (
    .A({MAR3, MAR2, MAR1, MAR0}), .Din(RML), .str(RMI), .C(CLK_t), .ld(1'b1), .D({RAM3, RAM2, RAM1, RAM0}));
  DipSwitch dipswitch_1 (.out(MD7));
  LED led_1 (.in(RAM7));
  and and_1 (and_1_out, II, CLK_t);
  Switch switch_1 (.A(1'b1), .B(nRUN));
  LED led_2 (.in(not_3_out));
  LED led_3 (.in(MAR3));
  assign B1 = RO ? RAM1 : 1'bz;  // Driver driver_2
  DipSwitch dipswitch_2 (.out(MD6));
  DipSwitch dipswitch_3 (.out(MD5));
  LED led_4 (.in(RAM6));
  LED led_5 (.in(RAM5));
  D_FF_AS #(.Bits(4)) d_ff_as_1 (
    .Set(1'b0), .D({B3, B2, B1, B0}), .C(and_1_out), .Clr(RST), .Q({IR3, IR2, IR1, IR0}));  // open: nQ
  D_FF_AS #(.Bits(4)) d_ff_as_2 (
    .Set(1'b0), .D({B7, B6, B5, B4}), .C(and_1_out), .Clr(RST), .Q({IR7, IR6, IR5, IR4}));  // open: nQ
  Switch switch_2 (.A(1'b1), .B(switch_2_b));
  LED led_6 (.in(switch_2_b));
  not not_1 (not_1_out, switch_2_b);
  not not_2 (not_2_out, switch_2_b);
  LED led_7 (.in(nRUN));
  not not_3 (not_3_out, nRUN);
  LED led_8 (.in(MAR1));
  LED led_9 (.in(MAR2));
  assign B3 = RO ? RAM3 : 1'bz;  // Driver driver_3
  assign B2 = RO ? RAM2 : 1'bz;  // Driver driver_4
  DipSwitch dipswitch_4 (.out(MD4));
  DipSwitch dipswitch_5 (.out(MD3));
  LED led_10 (.in(RAM4));
  LED led_11 (.in(RAM3));
  LED led_12 (.in(not_1_out));
  and and_2 (and_2_out, clk, switch_2_b);
  and and_3 (and_3_out, not_2_out, button_2_out);
  Multiplexer #(.Bits(4)) multiplexer_2 (
    .sel(nRUN), .in_0(d_ff_as_3_q), .in_1({MA3, MA2, MA1, MA0}), .out({MAR3, MAR2, MAR1, MAR0}));
  LED led_13 (.in(MAR0));
  assign B4 = RO ? RAM4 : 1'bz;  // Driver driver_5
  RAMDualPort #(.AddrBits(4), .Bits(4)) ramdualport_2 (
    .A({MAR3, MAR2, MAR1, MAR0}), .Din(RMH), .str(RMI), .C(CLK_t), .ld(1'b1), .D({RAM7, RAM6, RAM5, RAM4}));
  DipSwitch dipswitch_6 (.out(MD2));
  DipSwitch dipswitch_7 (.out(MD1));
  LED led_14 (.in(RAM2));
  LED led_15 (.in(RAM1));
  assign {B3, B2, B1, B0} = IO ? {IR3, IR2, IR1, IR0} : 4'bz;  // Driver driver_6
  LED led_16 (.in(IR7));
  or or_1 (or_1_out, and_2_out, and_3_out);
  not not_4 (not_4_out, HLT);
  assign B5 = RO ? RAM5 : 1'bz;  // Driver driver_7
  DipSwitch dipswitch_8 (.out(MD0));
  LED led_17 (.in(RAM0));
  LED led_18 (.in(IR6));
  LED led_19 (.in(IR5));
  and and_4 (CLK_t, or_1_out, not_4_out);
  DipSwitch dipswitch_9 (.out(MA3));
  DipSwitch dipswitch_10 (.out(MA2));
  and and_5 (and_5_out, MI, CLK_t);
  assign B7 = RO ? RAM7 : 1'bz;  // Driver driver_8
  assign B6 = RO ? RAM6 : 1'bz;  // Driver driver_9
  LED led_20 (.in(IR4));
  LED led_21 (.in(IR3));
  LED led_22 (.in(CLK_t));
  not not_5 (nCLK, CLK_t);
  DipSwitch dipswitch_11 (.out(MA1));
  DipSwitch dipswitch_12 (.out(MA0));
  D_FF_AS #(.Bits(4)) d_ff_as_3 (
    .Set(1'b0), .D({B3, B2, B1, B0}), .C(and_5_out), .Clr(RST), .Q(d_ff_as_3_q));  // open: nQ
  LED led_23 (.in(IR2));
  LED led_24 (.in(IR1));
  Multiplexer #(.Bits(4)) multiplexer_3 (.sel(nRUN), .in_0({B7, B6, B5, B4}), .in_1({MD7, MD6, MD5, MD4}), .out(RMH));
  Multiplexer #(.Bits(4)) multiplexer_4 (.sel(nRUN), .in_0({B3, B2, B1, B0}), .in_1({MD3, MD2, MD1, MD0}), .out(RML));
  LED led_25 (.in(IR0));
  and and_6 (and_6_out, BI, CLK_t);
  LED led_26 (.in(HLT));
  D_FF_AS #(.Bits(4)) d_ff_as_4 (
    .Set(1'b0), .D({B3, B2, B1, B0}), .C(and_6_out), .Clr(RST), .Q({BR3, BR2, BR1, BR0}));  // open: nQ
  D_FF_AS #(.Bits(4)) d_ff_as_5 (
    .Set(1'b0), .D({B7, B6, B5, B4}), .C(and_6_out), .Clr(RST), .Q({BR7, BR6, BR5, BR4}));  // open: nQ
  LED led_27 (.in(B7));
  LED led_28 (.in(RI));
  LED led_29 (.in(MI));
  CounterPreset #(.Bits(4)) counterpreset_1 (
    .en(CE), .C(CLK_t), .dir(1'b0), .in({B3, B2, B1, B0}), .ld(JMP), .clr(RST), .out(counterpreset_1_out));  // open: ovf
  LED led_30 (.in(B6));
  LED led_31 (.in(IO));
  LED led_32 (.in(RO));
  LED led_33 (.in(nCLK));
  xor xor_1 (xor_1_out, nCLK, RST);
  not not_6 (not_6_out, RST);
  LED led_34 (.in(BR7));
  LED led_35 (.in(counterpreset_1_out[3]));
  LED led_36 (.in(B5));
  LED led_37 (.in(AI));
  LED led_38 (.in(II));
  LED led_39 (.in(TC[2]));
  LED led_40 (.in(TC[1]));
  Counter #(.Bits(3)) counter_1 (.en(1'b1), .C(xor_1_out), .clr(driver_10_out), .out(TC));  // open: ovf
  assign driver_10_out = RST ? not_6_out : 1'bz;  // Driver driver_10
  not not_7 (T4, decoder_1_out_4);
  not not_8 (T5, decoder_1_out_5);
  not not_9 (T6, decoder_1_out_6);
  not not_10 (T7, decoder_1_out_7);
  LED led_41 (.in(BR6));
  LED led_42 (.in(BR5));
  LED led_43 (.in(counterpreset_1_out[1]));
  LED led_44 (.in(counterpreset_1_out[2]));
  LED led_45 (.in(B4));
  LED led_46 (.in(AO));
  LED led_47 (.in(TC[0]));
  PullDown #(.Bits(3)) pulldown_1 (.out(TC));
  Decoder #(.Selector_Bits(3)) decoder_1 (
    .sel(TC), .out_0(decoder_1_out_0), .out_1(decoder_1_out_1), .out_2(decoder_1_out_2),
    .out_3(decoder_1_out_3), .out_4(decoder_1_out_4), .out_5(decoder_1_out_5), .out_6(decoder_1_out_6),
    .out_7(decoder_1_out_7));
  not not_11 (T0, decoder_1_out_0);
  not not_12 (T1, decoder_1_out_1);
  not not_13 (T2, decoder_1_out_2);
  not not_14 (T3, decoder_1_out_3);
  LookUpTable #(.Bits(8)) lookuptable_1 (
    .in0(TC[0]), .in1(TC[1]), .in2(TC[2]), .in3(IR4), .in4(IR5), .in5(IR6), .in6(IR7), .in7(1'b0), .in8(ZFO),
    .in9(CFO), .in10(1'b0), .out({HLT, MI, RI, RO, IO, II, AI, AO}));
  LED led_48 (.in(BR4));
  LED led_49 (.in(BR3));
  LED led_50 (.in(counterpreset_1_out[0]));
  LED led_51 (.in(B3));
  LED led_52 (.in(EO));
  LED led_53 (.in(T0));
  LED led_54 (.in(BR2));
  LED led_55 (.in(BR1));
  assign B0 = CO ? counterpreset_1_out[0] : 1'bz;  // Driver driver_11
  assign B1 = CO ? counterpreset_1_out[1] : 1'bz;  // Driver driver_12
  assign B2 = CO ? counterpreset_1_out[2] : 1'bz;  // Driver driver_13
  assign B3 = CO ? counterpreset_1_out[3] : 1'bz;  // Driver driver_14
  LED led_56 (.in(B2));
  LED led_57 (.in(BI));
  LED led_58 (.in(SU));
  LED led_59 (.in(T2));
  LED led_60 (.in(T1));
  LED led_61 (.in(BR0));
  LED led_62 (.in(B1));
  LED led_63 (.in(CE));
  LED led_64 (.in(OI));
  LED led_65 (.in(T4));
  LED led_66 (.in(T3));
  LookUpTable #(.Bits(8)) lookuptable_2 (
    .in0(TC[0]), .in1(TC[1]), .in2(TC[2]), .in3(IR4), .in4(IR5), .in5(IR6), .in6(IR7), .in7(1'b0), .in8(ZFO),
    .in9(CFO), .in10(1'b0), .out({EO, SU, BI, OI, CE, CO, JMP, FI}));
  LED led_67 (.in(B0));
  LED led_68 (.in(JMP));
  LED led_69 (.in(CO));
  LED led_70 (.in(T5));
  LED led_71 (.in(T6));
  LED led_72 (.in(FI));
  LED led_73 (.in(T7));
  and and_7 (and_7_out, FI, CLK_t);
  LED led_74 (.in(CFO));
  Button button_3 (.out(RST));
  D_FF_AS #(.Bits(4)) d_ff_as_6 (
    .Set(1'b0), .D({2'b00, CF, ZF}), .C(and_7_out), .Clr(RST), .Q({d_ff_as_6_q, CFO, ZFO}));  // open: nQ
  LED led_75 (.in(ZFO));
  PullDown #(.Bits(4)) pulldown_2 (.out({d_ff_as_6_q, CFO, ZFO}));
  LED led_76 (.in(LL7));
  LED led_77 (.in(LL6));
  and and_8 (and_8_out, AI, CLK_t);
  xor xor_2 (xor_6_out[1], BR1, SU);
  xor xor_3 (xor_6_out[3], BR3, SU);
  xor xor_4 (xor_8_out[1], BR5, SU);
  xor xor_5 (xor_8_out[3], BR7, SU);
  LED led_78 (.in(LL5));
  LED led_79 (.in(LL4));
  D_FF_AS #(.Bits(4)) d_ff_as_7 (
    .Set(1'b0), .D({B3, B2, B1, B0}), .C(and_8_out), .Clr(RST), .Q({AR3, AR2, AR1, AR0}));  // open: nQ
  D_FF_AS #(.Bits(4)) d_ff_as_8 (
    .Set(1'b0), .D({B7, B6, B5, B4}), .C(and_8_out), .Clr(RST), .Q({AR7, AR6, AR5, AR4}));  // open: nQ
  xor xor_6 (xor_6_out[0], BR0, SU);
  xor xor_7 (xor_6_out[2], BR2, SU);
  xor xor_8 (xor_8_out[0], BR4, SU);
  xor xor_9 (xor_8_out[2], BR6, SU);
  LED led_80 (.in(LL3));
  LED led_81 (.in(LL2));
  and and_9 (and_9_out, OI, CLK_t);
  LED led_82 (.in(LL1));
  LED led_83 (.in(LL0));
  D_FF_AS #(.Bits(8)) d_ff_as_9 (
    .Set(1'b0), .D({B7, B6, B5, B4, B3, B2, B1, B0}), .C(and_9_out), .Clr(RST), .Q(d_ff_as_9_q));  // open: nQ
  JK_FF jk_ff_1 (.J(1'b1), .C(clk_2), .K(1'b1), .Q(jk_ff_1_q[0]));  // open: nQ
  JK_FF jk_ff_2 (.J(1'b1), .C(jk_ff_1_q[0]), .K(1'b1), .Q(jk_ff_1_q[1]));  // open: nQ
  assign {B3, B2, B1, B0} = AO ? {AR3, AR2, AR1, AR0} : 4'bz;  // Driver driver_15
  assign {B7, B6, B5, B4} = AO ? {AR7, AR6, AR5, AR4} : 4'bz;  // Driver driver_16
  assign B7 = EO ? LL7 : 1'bz;  // Driver driver_17
  LED led_84 (.in(AR7));
  Add #(.Bits(4)) add_1 (.a({AR7, AR6, AR5, AR4}), .b(xor_8_out), .c_i(add_2_c_o), .s({LL7, LL6, LL5, LL4}), .c_o(CF));
  assign B6 = EO ? LL6 : 1'bz;  // Driver driver_18
  assign B5 = EO ? LL5 : 1'bz;  // Driver driver_19
  EEPROM #(.AddrBits(11), .Bits(8)) eeprom_1 (
    .A({in_3, jk_ff_1_q, d_ff_as_9_q}), .CS(1'b1), .WE(1'b0), .OE(1'b1), .D(eeprom_1_d));
  LED led_85 (.in(AR6));
  LED led_86 (.in(AR5));
  assign B4 = EO ? LL4 : 1'bz;  // Driver driver_20
  LED led_87 (.in(AR4));
  LED led_88 (.in(AR3));
  Add #(.Bits(4)) add_2 (.a({AR3, AR2, AR1, AR0}), .b(xor_6_out), .c_i(SU), .s({LL3, LL2, LL1, LL0}), .c_o(add_2_c_o));
  assign B3 = EO ? LL3 : 1'bz;  // Driver driver_21
  LED led_89 (.in(AR2));
  LED led_90 (.in(AR1));
  assign B2 = EO ? LL2 : 1'bz;  // Driver driver_22
  assign B1 = EO ? LL1 : 1'bz;  // Driver driver_23
  Seven_Seg #(.commonCathode("true"), .ledPersistence("true")) seven_seg_1 (
    .a(eeprom_1_d[6]), .b(eeprom_1_d[5]), .c(eeprom_1_d[4]), .d(eeprom_1_d[3]), .e(eeprom_1_d[2]),
    .f(eeprom_1_d[1]), .g(eeprom_1_d[0]), .dp(1'b0), .common(not_18_out));
  LED led_91 (.in(AR0));
  assign B0 = EO ? LL0 : 1'bz;  // Driver driver_24
  Seven_Seg #(.commonCathode("true"), .ledPersistence("true")) seven_seg_2 (
    .a(eeprom_1_d[6]), .b(eeprom_1_d[5]), .c(eeprom_1_d[4]), .d(eeprom_1_d[3]), .e(eeprom_1_d[2]),
    .f(eeprom_1_d[1]), .g(eeprom_1_d[0]), .dp(1'b0), .common(not_17_out));
  nor nor_1 (ZF, LL0, LL1, LL2, LL3, LL4, LL5, LL6, LL7);
  Seven_Seg #(.commonCathode("true"), .ledPersistence("true")) seven_seg_3 (
    .a(eeprom_1_d[6]), .b(eeprom_1_d[5]), .c(eeprom_1_d[4]), .d(eeprom_1_d[3]), .e(eeprom_1_d[2]),
    .f(eeprom_1_d[1]), .g(eeprom_1_d[0]), .dp(1'b0), .common(not_16_out));
  not not_15 (not_15_out, decoder_2_out_0);
  not not_16 (not_16_out, decoder_2_out_1);
  not not_17 (not_17_out, decoder_2_out_2);
  not not_18 (not_18_out, decoder_2_out_3);
  Decoder #(.Selector_Bits(2)) decoder_2 (
    .sel(jk_ff_1_q), .out_0(decoder_2_out_0), .out_1(decoder_2_out_1), .out_2(decoder_2_out_2),
    .out_3(decoder_2_out_3));
  Seven_Seg #(.commonCathode("true"), .ledPersistence("true")) seven_seg_4 (
    .a(eeprom_1_d[6]), .b(eeprom_1_d[5]), .c(eeprom_1_d[4]), .d(eeprom_1_d[3]), .e(eeprom_1_d[2]),
    .f(eeprom_1_d[1]), .g(eeprom_1_d[0]), .dp(1'b0), .common(not_15_out));

  // Notes on the sheet:
  //   clk: Hz: 50
  //   clk_2: Hz: 50
  //   WRITE
  //   AUTO/MANUAL
  //   RUN/PROG
  //   Clock Module
  //   INSTRUCTION 
  //   REGISTER
  //   MEMORY ACCESS
  //   REGISTER
  //   RAM MODULE
  //   CONTROL WORD
  //   BUS
  //   contents of lookuptable_1 (hex, n*v repeats v):
  //   40,14,0,0,0,0,0,0,40,14,48,12,0,0,0,0,40,14,48,10,2,0,0,0,40,14,48,10,2,0,0,0,40,
  //   14,48,21,0,0,0,0,40,14,a,0,0,0,0,0,0,0,0,0,0,0,0,0,0,0,0,0,0,0,0,0,0,0,0,0,0,0,0,
  //   0,0,0,0,0,0,0,0,0,0,0,0,0,0,0,0,0,0,0,0,0,0,0,0,0,0,0,0,0,0,0,0,0,0,0,0,0,0,0,0,0,
  //   40,14,1,0,0,0,0,0,40,14,80
  //   B REGISTER
  //   PROGRAM
  //   COUNTER
  //   contents of lookuptable_2 (hex, n*v repeats v):
  //   4,8,0,0,0,0,0,0,4,8,0,0,0,0,0,0,4,8,0,20,80,0,0,0,4,8,0,20,c0,0,0,0,4,8,0,0,0,0,0,
  //   0,4,8,0,0,0,0,0,0,0,0,0,0,0,0,0,0,0,0,0,0,0,0,0,0,0,0,0,0,0,0,0,0,0,0,0,0,0,0,0,0,
  //   0,0,0,0,0,0,0,0,0,0,0,0,0,0,0,0,0,0,0,0,0,0,0,0,0,0,0,0,0,0,0,0,4,8,10,0,0,0,0,0,
  //   4,8
  //   MICROCODE
  //   EEPROMS
  //   MICRO
  //   INSTRUCTION
  //   COUNTER
  //   FLAG REGISTER
  //   contents of eeprom_1 (hex, n*v repeats v):
  //   7e,30,6d,79,33,5b,5f,70,7f,7b,7e,30,6d,79,33,5b,5f,70,7f,7b,7e,30,6d,79,33,5b,5f,
  //   70,7f,7b,7e,30,6d,79,33,5b,5f,70,7f,7b,7e,30,6d,79,33,5b,5f,70,7f,7b,7e,30,6d,79,
  //   33,5b,5f,70,7f,7b,7e,30,6d,79,33,5b,5f,70,7f,7b,7e,30,6d,79,33,5b,5f,70,7f,7b,7e,
  //   30,6d,79,33,5b,5f,70,7f,7b,7e,30,6d,79,33,5b,5f,70,7f,7b,7e,30,6d,79,33,5b,5f,70,
  //   7f,7b,7e,30,6d,79,33,5b,5f,70,7f,7b,7e,30,6d,79,33,5b,5f,70,7f,7b,7e,30,6d,79,33,
  //   5b,5f,70,7f,7b,7e,30,6d,79,33,5b,5f,70,7f,7b,7e,30,6d,79,33,5b,5f,70,7f,7b,7e,30,
  //   6d,79,33,5b,5f,70,7f,7b,7e,30,6d,79,33,5b,5f,70,7f,7b,7e,30,6d,79,33,5b,5f,70,7f,
  //   7b,7e,30,6d,79,33,5b,5f,70,7f,7b,7e,30,6d,79,33,5b,5f,70,7f,7b,7e,30,6d,79,33,5b,
  //   5f,70,7f,7b,7e,30,6d,79,33,5b,5f,70,7f,7b,7e,30,6d,79,33,5b,5f,70,7f,7b,7e,30,6d,
  //   79,33,5b,5f,70,7f,7b,7e,30,6d,79,33,5b,7e,7e,7e,7e,7e,7e,7e,7e,7e,7e,30,30,30,30,
  //   30,30,30,30,30,30,6d,6d,6d,6d,6d,6d,6d,6d,6d,6d,79,79,79,79,79,79,79,79,79,79,33,
  //   33,33,33,33,33,33,33,33,33,5b,5b,5b,5b,5b,5b,5b,5b,5b,5b,5f,5f,5f,5f,5f,5f,5f,5f,
  //   5f,5f,70,70,70,70,70,70,70,70,70,70,7f,7f,7f,7f,7f,7f,7f,7f,7f,7f,7b,7b,7b,7b,7b,
  //   7b,7b,7b,7b,7b,7e,7e,7e,7e,7e,7e,7e,7e,7e,7e,30,30,30,30,30,30,30,30,30,30,6d,6d,
  //   6d,6d,6d,6d,6d,6d,6d,6d,79,79,79,79,79,79,79,79,79,79,33,33,33,33,33,33,33,33,33,
  //   33,5b,5b,5b,5b,5b,5b,5b,5b,5b,5b,5f,5f,5f,5f,5f,5f,5f,5f,5f,5f,70,70,70,70,70,70,
  //   70,70,70,70,7f,7f,7f,7f,7f,7f,7f,7f,7f,7f,7b,7b,7b,7b,7b,7b,7b,7b,7b,7b,7e,7e,7e,
  //   7e,7e,7e,7e,7e,7e,7e,30,30,30,30,30,30,30,30,30,30,6d,6d,6d,6d,6d,6d,6d,6d,6d,6d,
  //   79,79,79,79,79,79,79,79,79,79,33,33,33,33,33,33,33,33,33,33,5b,5b,5b,5b,5b,5b,7e,
  //   7e,7e,7e,7e,7e,7e,7e,7e,7e,7e,7e,7e,7e,7e,7e,7e,7e,7e,7e,7e,7e,7e,7e,7e,7e,7e,7e,
  //   7e,7e,7e,7e,7e,7e,7e,7e,7e,7e,7e,7e,7e,7e,7e,7e,7e,7e,7e,7e,7e,7e,7e,7e,7e,7e,7e,
  //   7e,7e,7e,7e,7e,7e,7e,7e,7e,7e,7e,7e,7e,7e,7e,7e,7e,7e,7e,7e,7e,7e,7e,7e,7e,7e,7e,
  //   7e,7e,7e,7e,7e,7e,7e,7e,7e,7e,7e,7e,7e,7e,7e,7e,7e,7e,30,30,30,30,30,30,30,30,30,
  //   30,30,30,30,30,30,30,30,30,30,30,30,30,30,30,30,30,30,30,30,30,30,30,30,30,30,30,
  //   30,30,30,30,30,30,30,30,30,30,30,30,30,30,30,30,30,30,30,30,30,30,30,30,30,30,30,
  //   30,30,30,30,30,30,30,30,30,30,30,30,30,30,30,30,30,30,30,30,30,30,30,30,30,30,30,
  //   30,30,30,30,30,30,30,30,30,30,6d,6d,6d,6d,6d,6d,6d,6d,6d,6d,6d,6d,6d,6d,6d,6d,6d,
  //   6d,6d,6d,6d,6d,6d,6d,6d,6d,6d,6d,6d,6d,6d,6d,6d,6d,6d,6d,6d,6d,6d,6d,6d,6d,6d,6d,
  //   6d,6d,6d,6d,6d,6d,6d,6d,6d,6d,6d,6d,0,0,0,0,0,0,0,0,0,0,0,0,0,0,0,0,0,0,0,0,0,0,0,
  //   0,0,0,0,0,0,0,0,0,0,0,0,0,0,0,0,0,0,0,0,0,0,0,0,0,0,0,0,0,0,0,0,0,0,0,0,0,0,0,0,0,
  //   0,0,0,0,0,0,0,0,0,0,0,0,0,0,0,0,0,0,0,0,0,0,0,0,0,0,0,0,0,0,0,0,0,0,0,0,0,0,0,0,0,
  //   0,0,0,0,0,0,0,0,0,0,0,0,0,0,0,0,0,0,0,0,0,0,0,0,0,0,0,0,0,0,0,0,0,0,0,0,0,0,0,0,0,
  //   0,0,0,0,0,0,0,0,0,0,0,0,0,0,0,0,0,0,0,0,0,0,0,0,0,0,0,0,0,0,0,0,0,0,0,0,0,0,0,0,0,
  //   0,0,0,0,0,0,0,0,0,0,0,0,0,0,0,0,0,0,0,0,0,0,0,0,0,0,0,0,0,0,0,0,0,0,0,0,0,0,0,0,0,
  //   0,0,0,0,0,0,0,0,0,0,0,0,0,0,0,0,0,0,0,0,0,0,0,0,0,0,0,0,7f,70,5f,5b,33,79,6d,30,7e,
  //   7b,7f,70,5f,5b,33,79,6d,30,7e,7b,7f,70,5f,5b,33,79,6d,30,7e,7b,7f,70,5f,5b,33,79,
  //   6d,30,7e,7b,7f,70,5f,5b,33,79,6d,30,7e,7b,7f,70,5f,5b,33,79,6d,30,7e,7b,7f,70,5f,
  //   5b,33,79,6d,30,7e,7b,7f,70,5f,5b,33,79,6d,30,7e,7b,7f,70,5f,5b,33,79,6d,30,7e,7b,
  //   7f,70,5f,5b,33,79,6d,30,7e,7b,7f,70,5f,5b,33,79,6d,30,7e,7b,7f,70,5f,5b,33,79,6d,
  //   30,7e,7b,7f,70,5f,5b,33,79,6d,30,7e,30,6d,79,33,5b,5f,70,7f,7b,7e,30,6d,79,33,5b,
  //   5f,70,7f,7b,7e,30,6d,79,33,5b,5f,70,7f,7b,7e,30,6d,79,33,5b,5f,70,7f,7b,7e,30,6d,
  //   79,33,5b,5f,70,7f,7b,7e,30,6d,79,33,5b,5f,70,7f,7b,7e,30,6d,79,33,5b,5f,70,7f,7b,
  //   7e,30,6d,79,33,5b,5f,70,7f,7b,7e,30,6d,79,33,5b,5f,70,7f,7b,7e,30,6d,79,33,5b,5f,
  //   70,7f,7b,7e,30,6d,79,33,5b,5f,70,7f,7b,7e,30,6d,79,33,5b,5f,70,7f,7b,7e,30,6d,79,
  //   33,5b,5f,70,6d,6d,6d,6d,6d,6d,6d,6d,6d,30,30,30,30,30,30,30,30,30,30,7e,7e,7e,7e,
  //   7e,7e,7e,7e,7e,7e,7b,7b,7b,7b,7b,7b,7b,7b,7b,7b,7f,7f,7f,7f,7f,7f,7f,7f,7f,7f,70,
  //   70,70,70,70,70,70,70,70,70,5f,5f,5f,5f,5f,5f,5f,5f,5f,5f,5b,5b,5b,5b,5b,5b,5b,5b,
  //   5b,5b,33,33,33,33,33,33,33,33,33,33,79,79,79,79,79,79,79,79,79,79,6d,6d,6d,6d,6d,
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  //   A REGISTER
  //   ALU MODULE
  //   OUTPUT
endmodule
